# Fritzing sketch ECAD (saved by Fritzing 0.9.3b)
breadboards: 1

parts:
  LCD1 = LCD screen
  Part1 = Arduino Uno (Rev3)
  U1 = POT_SWITCH [package=pot_pth]

nets:
  VSS: LCD1.VSS, LCD1.R/W, LCD1.LED-, Part1.GND
  VDD: LCD1.VDD, LCD1.LED+, Part1.5V, U1.G$1_A
  N1: LCD1.V0, U1.G$2_1
  N2: LCD1.RS, Part1.D12/MISO
  N3: LCD1.E, Part1.D2
  N4: LCD1.DB4, Part1.D4
  N5: LCD1.DB5, Part1.D5_PWM
  N6: LCD1.DB6, Part1.D6_PWM
  N7: LCD1.DB7, Part1.D7
